// Logisim project CPU.circ as structural Verilog: 7 circuits, main circuit main
module main (
  input  reset,
  input  clock_input_1,
  input  clock_enable
);

  wire alu_1_zero, and_1_out, and_2_out, clock_input_out, control_unit_1_alusrc, control_unit_1_branch,
       control_unit_1_jump, control_unit_1_memtoreg, control_unit_1_memwrite, control_unit_1_regdst,
       control_unit_1_regwrite, or_1_out;
  wire [2:0] control_unit_1_alucontrol;
  wire [4:0] multiplexer_3_out;
  wire [7:0] instructions_memory_p2, instructions_memory_p3, instructions_memory_p4, instructions_memory_p5;
  wire [15:0] adder_1_out, adder_2_out, fetch_register_1_pcplus4o, multiplexer_1_out, multiplexer_2_out,
       register_1_q, shifter_1_out, shifter_2_out, shifter_3_out;
  wire [31:0] alu_1_result, bit_extender_1_out, data_memory_dout, fetch_register_1_instrdo,
       multiplexer_4_out, multiplexer_5_out, register_file_1_rd1, register_file_1_rd2;

  Clock clock_input (.out(clock_input_out));
  and and_1 (and_1_out, clock_input_out, clock_enable);
  or or_1 (or_1_out, clock_input_1, and_1_out);
  Multiplexer #(.width(16)) multiplexer_1 (
    .in0(multiplexer_2_out), .in1(shifter_3_out), .out(multiplexer_1_out), .sel(control_unit_1_jump));
  Multiplexer #(.width(16)) multiplexer_2 (
    .in0(adder_1_out), .in1(adder_2_out), .out(multiplexer_2_out), .sel(and_2_out));
  Register #(.width(16)) register_1 (.D(multiplexer_1_out), .en(1'b1), .clk(or_1_out), .Q(register_1_q), .clr(reset));
  // ROM #(.addrWidth(16), .line("quad")) instructions_memory: pin names not known; wires that end beside it: register_1_q, instructions_memory_p2, instructions_memory_p3, instructions_memory_p4, instructions_memory_p5
  Adder #(.width(16)) adder_1 (.a(register_1_q), .b(16'h4), .out(adder_1_out));  // open: cin, cout
  fetch_register fetch_register_1 (
    .WE(1'b1), .clock(or_1_out), .reset(reset),
    .instrDi({instructions_memory_p5, instructions_memory_p4, instructions_memory_p3, instructions_memory_p2}),
    .PCPlus4i(register_1_q), .instrDo(fetch_register_1_instrdo), .PCPlus4o(fetch_register_1_pcplus4o));
  assign bit_extender_1_out = {{16{fetch_register_1_instrdo[15]}}, fetch_register_1_instrdo[15:0]};  // Bit_Extender bit_extender_1
  Shifter #(.width(16)) shifter_1 (.in(fetch_register_1_instrdo[15:0]), .\dist (4'b0010), .out(shifter_1_out));
  Shifter #(.shift("lr"), .width(16)) shifter_2 (
    .in(fetch_register_1_instrdo[15:0]), .\dist (4'b0010), .out(shifter_2_out));
  control_unit control_unit_1 (
    .opcode(fetch_register_1_instrdo[31:26]), .funct(fetch_register_1_instrdo[5:0]),
    .Jump(control_unit_1_jump), .MemtoReg(control_unit_1_memtoreg), .MemWrite(control_unit_1_memwrite),
    .Branch(control_unit_1_branch), .ALUControl(control_unit_1_alucontrol), .ALUSrc(control_unit_1_alusrc),
    .RegDst(control_unit_1_regdst), .RegWrite(control_unit_1_regwrite));
  Adder #(.width(16)) adder_2 (.a(shifter_1_out), .b(fetch_register_1_pcplus4o), .out(adder_2_out));  // open: cin, cout
  Shifter #(.width(16)) shifter_3 (.in(shifter_2_out), .\dist (4'b0010), .out(shifter_3_out));
  register_file register_file_1 (
    .clock(or_1_out), .WE3(control_unit_1_regwrite), .reset(reset), .A1(fetch_register_1_instrdo[25:21]),
    .A2(fetch_register_1_instrdo[20:16]), .A3(multiplexer_3_out), .WD3(multiplexer_5_out),
    .RD1(register_file_1_rd1), .RD2(register_file_1_rd2));
  Multiplexer #(.width(5)) multiplexer_3 (
    .in0(fetch_register_1_instrdo[20:16]), .in1(fetch_register_1_instrdo[15:11]), .out(multiplexer_3_out),
    .sel(control_unit_1_regdst));
  Multiplexer #(.width(32)) multiplexer_4 (
    .in0(register_file_1_rd2), .in1(bit_extender_1_out), .out(multiplexer_4_out), .sel(control_unit_1_alusrc));
  and and_2 (and_2_out, control_unit_1_branch, alu_1_zero);
  ALU alu_1 (
    .Select_pin(control_unit_1_alucontrol), .Data_0(register_file_1_rd1), .Data_1(multiplexer_4_out),
    .zero(alu_1_zero), .Result(alu_1_result));
  RAM #(.addrWidth(16), .asyncread("true"), .clearpin("true"), .dataWidth(32)) data_memory (
    .addr(alu_1_result[15:0]), .we(control_unit_1_memwrite), .oe(1'b1), .clk(or_1_out),
    .din(register_file_1_rd2), .dout(data_memory_dout), .clr(reset));
  Multiplexer #(.width(32)) multiplexer_5 (
    .in0(alu_1_result), .in1(data_memory_dout), .out(multiplexer_5_out), .sel(control_unit_1_memtoreg));

  // Notes on the sheet:
  //   contents of instructions_memory (hex, n*v repeats v):
  //   2 0 21 20 1 0 42 20 1 0 1 ac 2 0 2 ac 1c 0 0 8 5 0 63 20 2 0 63 20 1 0 63 20 3 0 63 20 3 0 3 ac
endmodule

module ALU (
  input  [2:0] Select_pin,
  input  [31:0] Data_0,
  input  [31:0] Data_1,
  output zero,
  output [31:0] Result
);

  wire [0:0] comparator_1_lt;
  wire [31:0] adder_1_out, and_1_out, demultiplexer_1_out0, demultiplexer_1_out1, demultiplexer_1_out2,
       demultiplexer_1_out6, demultiplexer_1_out7, demultiplexer_2_out0, demultiplexer_2_out1,
       demultiplexer_2_out2, demultiplexer_2_out6, demultiplexer_2_out7, or_1_out, subtractor_1_out;

  Demultiplexer #(.select(3), .tristate("true"), .width(32)) demultiplexer_1 (
    .out0(demultiplexer_1_out0), .out1(demultiplexer_1_out1), .out2(demultiplexer_1_out2),
    .out6(demultiplexer_1_out6), .out7(demultiplexer_1_out7), .in(Data_0), .sel(Select_pin));  // open: out3, out4, out5
  Demultiplexer #(.select(3), .tristate("true"), .width(32)) demultiplexer_2 (
    .out0(demultiplexer_2_out0), .out1(demultiplexer_2_out1), .out2(demultiplexer_2_out2),
    .out6(demultiplexer_2_out6), .out7(demultiplexer_2_out7), .in(Data_1), .sel(Select_pin));  // open: out3, out4, out5
  assign and_1_out = demultiplexer_1_out0 & demultiplexer_2_out0;  // AND_Gate and_1, 32 bits wide
  assign or_1_out = demultiplexer_1_out1 | demultiplexer_2_out1;  // OR_Gate or_1, 32 bits wide
  Adder #(.width(32)) adder_1 (
    .a(demultiplexer_1_out2), .b(demultiplexer_2_out2), .out(adder_1_out));  // open: cin, cout
  Subtractor #(.width(32)) subtractor_1 (
    .a(demultiplexer_1_out6), .b(demultiplexer_2_out6), .out(subtractor_1_out));  // open: bin, bout
  Comparator #(.width(32)) comparator_1 (
    .a(demultiplexer_1_out7), .b(demultiplexer_2_out7), .lt(comparator_1_lt[0]));  // open: gt, eq
  Multiplexer #(.select(3), .width(32)) multiplexer_1 (
    .in0(and_1_out), .in1(or_1_out), .in2(adder_1_out), .in6(subtractor_1_out),
    .in7({{31{1'b0}}, comparator_1_lt[0]}), .out(Result), .sel(Select_pin));  // open: in3, in4, in5
  Comparator #(.width(32)) comparator_2 (.a({32{1'b0}}), .b(Result), .eq(zero));  // open: gt, lt
endmodule

module register_file (
  input  clock,
  input  WE3,
  input  reset,
  input  [4:0] A1,
  input  [4:0] A2,
  input  [4:0] A3,
  input  [31:0] WD3,
  output [31:0] RD1,
  output [31:0] RD2
);

  wire DMX0, DMX1, DMX2, DMX3, DMX4, DMX5, DMX6, DMX7, DMX8, DMX9, DMX10, DMX11, DMX12, DMX13, DMX14, DMX15,
       DMX16, DMX17, DMX18, DMX19, DMX20, DMX21, DMX22, DMX23, DMX24, DMX25, DMX26, DMX27, DMX28, DMX29,
       DMX30, DMX31;
  wire [31:0] register_1_q, register_2_q, register_3_q, register_4_q, register_5_q, register_6_q,
       register_7_q, register_8_q, register_9_q, register_10_q, register_11_q, register_12_q, register_13_q,
       register_14_q, register_15_q, register_16_q, register_17_q, register_18_q, register_19_q,
       register_20_q, register_21_q, register_22_q, register_23_q, register_24_q, register_25_q,
       register_26_q, register_27_q, register_28_q, register_29_q, register_30_q, register_31_q;

  Register #(.width(32)) register_1 (.D(WD3), .en(DMX1), .clk(clock), .Q(register_1_q), .clr(reset));
  Register #(.width(32)) register_2 (.D(WD3), .en(DMX2), .clk(clock), .Q(register_2_q), .clr(reset));
  Register #(.width(32)) register_3 (.D(WD3), .en(DMX3), .clk(clock), .Q(register_3_q), .clr(reset));
  Register #(.width(32)) register_4 (.D(WD3), .en(DMX4), .clk(clock), .Q(register_4_q), .clr(reset));
  Register #(.width(32)) register_5 (.D(WD3), .en(DMX5), .clk(clock), .Q(register_5_q), .clr(reset));
  Register #(.width(32)) register_6 (.D(WD3), .en(DMX6), .clk(clock), .Q(register_6_q), .clr(reset));
  Register #(.width(32)) register_7 (.D(WD3), .en(DMX7), .clk(clock), .Q(register_7_q), .clr(reset));
  Demultiplexer #(.select(5)) demultiplexer_1 (
    .out0(DMX0), .out1(DMX1), .out2(DMX2), .out3(DMX3), .out4(DMX4), .out5(DMX5), .out6(DMX6), .out7(DMX7),
    .out8(DMX8), .out9(DMX9), .out10(DMX10), .out11(DMX11), .out12(DMX12), .out13(DMX13), .out14(DMX14),
    .out15(DMX15), .out16(DMX16), .out17(DMX17), .out18(DMX18), .out19(DMX19), .out20(DMX20), .out21(DMX21),
    .out22(DMX22), .out23(DMX23), .out24(DMX24), .out25(DMX25), .out26(DMX26), .out27(DMX27), .out28(DMX28),
    .out29(DMX29), .out30(DMX30), .out31(DMX31), .in(WE3), .sel(A3));
  Register #(.width(32)) register_8 (.D(WD3), .en(DMX8), .clk(clock), .Q(register_8_q), .clr(reset));
  Register #(.width(32)) register_9 (.D(WD3), .en(DMX9), .clk(clock), .Q(register_9_q), .clr(reset));
  Register #(.width(32)) register_10 (.D(WD3), .en(DMX10), .clk(clock), .Q(register_10_q), .clr(reset));
  Register #(.width(32)) register_11 (.D(WD3), .en(DMX11), .clk(clock), .Q(register_11_q), .clr(reset));
  Register #(.width(32)) register_12 (.D(WD3), .en(DMX12), .clk(clock), .Q(register_12_q), .clr(reset));
  Register #(.width(32)) register_13 (.D(WD3), .en(DMX13), .clk(clock), .Q(register_13_q), .clr(reset));
  Register #(.width(32)) register_14 (.D(WD3), .en(DMX14), .clk(clock), .Q(register_14_q), .clr(reset));
  Register #(.width(32)) register_15 (.D(WD3), .en(DMX15), .clk(clock), .Q(register_15_q), .clr(reset));
  Register #(.width(32)) register_16 (.D(WD3), .en(DMX16), .clk(clock), .Q(register_16_q), .clr(reset));
  Register #(.width(32)) register_17 (.D(WD3), .en(DMX17), .clk(clock), .Q(register_17_q), .clr(reset));
  Register #(.width(32)) register_18 (.D(WD3), .en(DMX18), .clk(clock), .Q(register_18_q), .clr(reset));
  Register #(.width(32)) register_19 (.D(WD3), .en(DMX19), .clk(clock), .Q(register_19_q), .clr(reset));
  Register #(.width(32)) register_20 (.D(WD3), .en(DMX20), .clk(clock), .Q(register_20_q), .clr(reset));
  Register #(.width(32)) register_21 (.D(WD3), .en(DMX21), .clk(clock), .Q(register_21_q), .clr(reset));
  Register #(.width(32)) register_22 (.D(WD3), .en(DMX22), .clk(clock), .Q(register_22_q), .clr(reset));
  Register #(.width(32)) register_23 (.D(WD3), .en(DMX23), .clk(clock), .Q(register_23_q), .clr(reset));
  Register #(.width(32)) register_24 (.D(WD3), .en(DMX24), .clk(clock), .Q(register_24_q), .clr(reset));
  Register #(.width(32)) register_25 (.D(WD3), .en(DMX25), .clk(clock), .Q(register_25_q), .clr(reset));
  Register #(.width(32)) register_26 (.D(WD3), .en(DMX26), .clk(clock), .Q(register_26_q), .clr(reset));
  Register #(.width(32)) register_27 (.D(WD3), .en(DMX27), .clk(clock), .Q(register_27_q), .clr(reset));
  Register #(.width(32)) register_28 (.D(WD3), .en(DMX28), .clk(clock), .Q(register_28_q), .clr(reset));
  Register #(.width(32)) register_29 (.D(WD3), .en(DMX29), .clk(clock), .Q(register_29_q), .clr(reset));
  Register #(.width(32)) register_30 (.D(WD3), .en(DMX30), .clk(clock), .Q(register_30_q), .clr(reset));
  Register #(.width(32)) register_31 (.D(WD3), .en(DMX31), .clk(clock), .Q(register_31_q), .clr(reset));
  Multiplexer #(.select(5), .width(32)) multiplexer_1 (
    .in0({32{1'b0}}), .in1(register_1_q), .in2(register_2_q), .in3(register_3_q), .in4(register_4_q),
    .in5(register_5_q), .in6(register_6_q), .in7(register_7_q), .in8(register_8_q), .in9(register_9_q),
    .in10(register_10_q), .in11(register_11_q), .in12(register_12_q), .in13(register_13_q),
    .in14(register_14_q), .in15(register_15_q), .in16(register_16_q), .in17(register_17_q),
    .in18(register_18_q), .in19(register_19_q), .in20(register_20_q), .in21(register_21_q),
    .in22(register_22_q), .in23(register_23_q), .in24(register_24_q), .in25(register_25_q),
    .in26(register_26_q), .in27(register_27_q), .in28(register_28_q), .in29(register_29_q),
    .in30(register_30_q), .in31(register_31_q), .out(RD1), .sel(A1));
  Multiplexer #(.select(5), .width(32)) multiplexer_2 (
    .in0({32{1'b0}}), .in1(register_1_q), .in2(register_2_q), .in3(register_3_q), .in4(register_4_q),
    .in5(register_5_q), .in6(register_6_q), .in7(register_7_q), .in8(register_8_q), .in9(register_9_q),
    .in10(register_10_q), .in11(register_11_q), .in12(register_12_q), .in13(register_13_q),
    .in14(register_14_q), .in15(register_15_q), .in16(register_16_q), .in17(register_17_q),
    .in18(register_18_q), .in19(register_19_q), .in20(register_20_q), .in21(register_21_q),
    .in22(register_22_q), .in23(register_23_q), .in24(register_24_q), .in25(register_25_q),
    .in26(register_26_q), .in27(register_27_q), .in28(register_28_q), .in29(register_29_q),
    .in30(register_30_q), .in31(register_31_q), .out(RD2), .sel(A2));
endmodule

module control_unit (
  input  [5:0] opcode,
  input  [5:0] funct,
  output Jump,
  output MemtoReg,
  output MemWrite,
  output Branch,
  output [2:0] ALUControl,
  output ALUSrc,
  output RegDst,
  output RegWrite
);

  wire [1:0] control_unit_main_decoder_1_aluop;

  control_unit_main_decoder control_unit_main_decoder_1 (
    .opcode(opcode), .Jump(Jump), .RegWrite(RegWrite), .RegDst(RegDst), .ALUSrc(ALUSrc), .Branch(Branch),
    .MemWrite(MemWrite), .MemtoReg(MemtoReg), .ALUOp(control_unit_main_decoder_1_aluop));
  control_unit_alu_decoder control_unit_alu_decoder_1 (
    .ALUOp(control_unit_main_decoder_1_aluop), .funct(funct), .ALUControl(ALUControl));
endmodule

module control_unit_main_decoder (
  input  [5:0] opcode,
  output Jump,
  output RegWrite,
  output RegDst,
  output ALUSrc,
  output Branch,
  output MemWrite,
  output MemtoReg,
  output [1:0] ALUOp
);

  wire comparator_1_eq, comparator_2_eq, comparator_3_eq, comparator_4_eq, comparator_5_eq, comparator_6_eq,
       comparator_7_eq;

  Comparator #(.width(6)) comparator_1 (.a({6{1'b0}}), .b(opcode), .eq(comparator_1_eq));  // open: gt, lt
  Comparator #(.width(6)) comparator_2 (.a(6'b100011), .b(opcode), .eq(comparator_2_eq));  // open: gt, lt
  Comparator #(.width(6)) comparator_3 (.a(6'b101011), .b(opcode), .eq(comparator_3_eq));  // open: gt, lt
  Comparator #(.width(6)) comparator_4 (.a(6'b000100), .b(opcode), .eq(comparator_4_eq));  // open: gt, lt
  Comparator #(.width(6)) comparator_5 (.a(6'b001000), .b(opcode), .eq(comparator_5_eq));  // open: gt, lt
  Comparator #(.width(6)) comparator_6 (.a(6'b001001), .b(opcode), .eq(comparator_6_eq));  // open: gt, lt
  Comparator #(.width(6)) comparator_7 (.a(6'b000010), .b(opcode), .eq(comparator_7_eq));  // open: gt, lt
  buf or_1 (Jump, comparator_7_eq);  // OR_Gate
  or or_2 (RegWrite, comparator_1_eq, comparator_2_eq, comparator_5_eq, comparator_6_eq);
  buf or_3 (RegDst, comparator_1_eq);  // OR_Gate
  or or_4 (ALUSrc, comparator_2_eq, comparator_3_eq, comparator_5_eq, comparator_6_eq);
  buf or_5 (Branch, comparator_4_eq);  // OR_Gate
  buf or_6 (MemWrite, comparator_3_eq);  // OR_Gate
  buf or_7 (MemtoReg, comparator_2_eq);  // OR_Gate
  buf ALUOp1 (ALUOp[1], comparator_1_eq);  // OR_Gate
  or ALUOp0 (ALUOp[0], comparator_4_eq, comparator_6_eq);

  // Notes on the sheet:
  //   lw
  //   sw
  //   beq
  //   addi
  //   subi
  //   j
  //   R-type
endmodule

module control_unit_alu_decoder (
  input  [1:0] ALUOp,
  input  [5:0] funct,
  output [2:0] ALUControl
);

  wire comparator_1_eq, comparator_2_eq, comparator_3_eq, comparator_4_eq, comparator_5_eq, comparator_6_eq,
       comparator_7_eq, comparator_8_eq, comparator_9_eq, or_1_out;
  wire [2:0] controlled_buffer_1_out, controlled_buffer_2_out;

  Comparator #(.mode("unsigned"), .width(2)) comparator_1 (.a(2'b00), .b(ALUOp), .eq(comparator_1_eq));  // open: gt, lt
  Comparator #(.mode("unsigned"), .width(2)) comparator_2 (.a(ALUOp), .b(2'b01), .eq(comparator_2_eq));  // open: gt, lt
  Comparator #(.mode("unsigned"), .width(2)) comparator_3 (.a(ALUOp), .b(2'b10), .eq(comparator_3_eq));  // open: gt, lt
  Comparator #(.mode("unsigned"), .width(2)) comparator_4 (.a(ALUOp), .b(2'b11), .eq(comparator_4_eq));  // open: gt, lt
  Comparator #(.mode("unsigned"), .width(6)) comparator_5 (
    .a(6'b100000), .b(funct), .eq(comparator_5_eq));  // open: gt, lt
  Comparator #(.mode("unsigned"), .width(6)) comparator_6 (
    .a(6'b100010), .b(funct), .eq(comparator_6_eq));  // open: gt, lt
  Comparator #(.mode("unsigned"), .width(6)) comparator_7 (
    .a(6'b100100), .b(funct), .eq(comparator_7_eq));  // open: gt, lt
  Comparator #(.mode("unsigned"), .width(6)) comparator_8 (
    .a(6'b100101), .b(funct), .eq(comparator_8_eq));  // open: gt, lt
  Comparator #(.mode("unsigned"), .width(6)) comparator_9 (
    .a(6'b101010), .b(funct), .eq(comparator_9_eq));  // open: gt, lt
  assign controlled_buffer_1_out = comparator_1_eq ? 3'b010 : 3'bz;  // Controlled_Buffer controlled_buffer_1
  assign controlled_buffer_2_out = comparator_5_eq ? 3'b010 : 3'bz;  // Controlled_Buffer controlled_buffer_2
  assign controlled_buffer_2_out = comparator_6_eq ? 3'b110 : 3'bz;  // Controlled_Buffer controlled_buffer_3
  assign controlled_buffer_2_out = comparator_7_eq ? 3'b000 : 3'bz;  // Controlled_Buffer controlled_buffer_4
  assign controlled_buffer_2_out = comparator_8_eq ? 3'b001 : 3'bz;  // Controlled_Buffer controlled_buffer_5
  assign controlled_buffer_2_out = comparator_9_eq ? 3'b111 : 3'bz;  // Controlled_Buffer controlled_buffer_6
  or or_1 (or_1_out, comparator_2_eq, comparator_4_eq);
  assign controlled_buffer_1_out = or_1_out ? 3'b110 : 3'bz;  // Controlled_Buffer controlled_buffer_7
  Multiplexer #(.width(3)) multiplexer_1 (
    .in0(controlled_buffer_1_out), .in1(controlled_buffer_2_out), .out(ALUControl), .sel(comparator_3_eq));

  // Notes on the sheet:
  //   00
  //   01
  //   10
  //   11
  //   add
  //   sub
  //   and
  //   or
  //   slt
endmodule

module fetch_register (
  input  WE,
  input  clock,
  input  reset,
  input  [31:0] instrDi,
  input  [15:0] PCPlus4i,
  output [31:0] instrDo,
  output [15:0] PCPlus4o
);

  Register #(.width(32)) register_1 (.D(instrDi), .en(WE), .clk(clock), .Q(instrDo), .clr(reset));
  Register #(.width(16)) register_2 (.D(PCPlus4i), .en(WE), .clk(clock), .Q(PCPlus4o), .clr(reset));
endmodule
